// Digital circuit ALU.dig as structural Verilog
module ALU (
  input  [5:0] operation,
  input  [31:0] src1,
  input  [31:0] src2,
  input  [2:0] func3,
  input  [6:0] func7,
  output [31:0] Result,
  output [31:0] Zero,
  output [31:0] Overflow,
  output CarryOut
);

  wire ADDER_c_o, and_3_out, comparator_1_eq, comparator_2_eq, SUBSTRACTOR_c_o;
  wire [0:0] SLT__signed_lt, SLT__unsigned_lt;
  wire [6:0] and_2_out;
  wire [31:0] ADDER_s, and_1_out, MUL_mul, multiplexer_1_out, multiplexer_2_out, multiplexer_3_out, or_1_out,
       SLL_out, SRA_out, SRL_out, SUBSTRACTOR_s, xor_1_out;

  Comparator #(.Bits(32)) SLT__unsigned (.a(src1), .b(src2), .lt(SLT__unsigned_lt[0]));  // open: gt, eq
  Comparator #(.Signed("true"), .Bits(32)) SLT__signed (.a(src1), .b(src2), .lt(SLT__signed_lt[0]));  // open: gt, eq
  assign and_1_out = src2 & src1;  // And and_1, 32 bits wide
  assign or_1_out = src1 | src2;  // Or or_1, 32 bits wide
  Mul #(.Bits(16)) MUL (.a(src1[15:0]), .b(src2[15:0]), .mul(MUL_mul));
  assign xor_1_out = src1 ^ src2;  // XOr xor_1, 32 bits wide
  BarrelShifter #(.Bits(32)) SLL (.in(src1), .shift(src2[5:0]), .out(SLL_out));
  BarrelShifter #(.Bits(32), .direction("right")) SRL (.in(src1), .shift(src2[5:0]), .out(SRL_out));
  BarrelShifter #(.Bits(32), .barrelShifterMode("arithmetic"), .direction("right")) SRA (
    .in(src1), .shift(src2[5:0]), .out(SRA_out));
  assign and_2_out = ~{3'b000, operation[3:0]} & ~func7;  // And and_2, 7 bits wide
  Add #(.Bits(32)) ADDER (.a(src1), .b(src2), .c_i(1'b0), .s(ADDER_s), .c_o(ADDER_c_o));
  Sub #(.Bits(32)) SUBSTRACTOR (.a(src1), .b(src2), .c_i(1'b0), .s(SUBSTRACTOR_s), .c_o(SUBSTRACTOR_c_o));
  Comparator #(.Bits(7)) comparator_1 (.a(and_2_out), .b({7{1'b1}}), .eq(comparator_1_eq));  // open: gt, lt
  and and_3 (and_3_out, func3[1], operation[5], 1'b1);
  Multiplexer #(.Bits(32)) multiplexer_1 (
    .sel(and_3_out), .in_0(ADDER_s), .in_1({{31{1'b0}}, SLT__signed_lt[0]}), .out(multiplexer_1_out));
  Multiplexer #(.Bits(32)) multiplexer_2 (
    .sel(comparator_2_eq), .in_0(SUBSTRACTOR_s), .in_1(ADDER_s), .out(multiplexer_2_out));
  Comparator #(.Bits(7)) comparator_2 (.a({7{1'b1}}), .b(func7), .eq(comparator_2_eq));  // open: gt, lt
  Multiplexer #(.Bits(32)) multiplexer_3 (
    .sel(comparator_1_eq), .in_0(MUL_mul), .in_1(ADDER_s), .out(multiplexer_3_out));
  Multiplexer #(.Selector_Bits(4), .Bits(32)) multiplexer_4 (
    .sel(operation[3:0]), .in_0(multiplexer_3_out), .in_1(SLL_out), .in_2(multiplexer_1_out),
    .in_3({{31{1'b0}}, SLT__unsigned_lt[0]}), .in_4(xor_1_out), .in_5(SRL_out), .in_6(or_1_out),
    .in_7(and_1_out), .in_8(multiplexer_2_out), .in_9({32{1'b0}}), .in_10({32{1'b0}}), .in_11({32{1'b0}}),
    .in_12({32{1'b0}}), .in_13(SRA_out), .in_14({32{1'b0}}), .in_15({32{1'b0}}), .out(Overflow));
  Multiplexer #(.Selector_Bits(4)) multiplexer_5 (
    .sel(operation[3:0]), .in_0(ADDER_c_o), .in_1(1'b0), .in_2(1'b0), .in_3(1'b0), .in_4(1'b0), .in_5(1'b0),
    .in_6(1'b0), .in_7(1'b0), .in_8(SUBSTRACTOR_c_o), .in_9(1'b0), .in_10(1'b0), .in_11(1'b0), .in_12(1'b0),
    .in_13(1'b0), .in_14(1'b0), .in_15(1'b0), .out(CarryOut));

  assign Result = Overflow;
  assign Zero = Overflow;

  // Notes on the sheet:
  //   ALU OP
  //   Sum
  //   Carry out
endmodule
