// Digital circuit Alu Control Unit.dig as structural Verilog
module Alu_Control_Unit (
  input  [3:0] Control_in,
  input  [1:0] Alu_op,
  output [5:0] Operation
);


  assign Operation = {Alu_op, Control_in};
endmodule
