// Digital circuit ImmediateGen.dig as structural Verilog
module ImmediateGen (
  input  [31:0] instr,
  output [31:0] immidiate
);

  wire and_3_out, not_1_out, not_2_out;
  wire [2:1] and_1_out;

  not not_1 (not_1_out, instr[5]);
  not not_2 (not_2_out, instr[6]);
  and and_1 (and_1_out[1], not_1_out, not_2_out);
  and and_2 (and_1_out[2], not_2_out, instr[5]);
  Multiplexer #(.Selector_Bits(3), .Bits(12)) multiplexer_1 (
    .sel({and_1_out, instr[6]}), .in_0({12{1'b0}}), .in_1({instr[31], instr[7], instr[30:25], instr[11:8]}),
    .in_2(instr[31:20]), .in_3({12{1'b0}}), .in_4({instr[31:25], instr[11:7]}), .in_5({12{1'b0}}),
    .in_6({12{1'b0}}), .in_7({12{1'b0}}), .out(immidiate[11:0]));
  and and_3 (and_3_out, immidiate[11], 1'b1);
  Multiplexer #(.Bits(20)) multiplexer_2 (
    .sel(and_3_out), .in_0({20{1'b0}}), .in_1({20{1'b1}}), .out(immidiate[31:12]));

  // Notes on the sheet:
  //   Load immediate
  //   Store immediate
  //   Branch immediate
endmodule
