// Digital circuit InstructionDecoder.dig as structural Verilog
module InstructionDecoder (
  input  [31:0] inst,
  output [6:0] opcode_6_0,
  output [4:0] rd_inst_11_7,
  output [4:0] rs1_inst_19_15,
  output [4:0] rs2_inst_24_20,
  output [6:0] func7,
  output [31:0] inst_31_0,
  output [2:0] funct3,
  output [11:0] imm,
  output Branch,
  output MemRead,
  output MemToReg,
  output [1:0] ALUOp,
  output MemWrite,
  output ALUSrc,
  output RegWrite
);

  wire decoder_1_out_4;

  Decoder #(.Selector_Bits(5)) decoder_1 (
    .sel(inst[6:2]), .out_0(MemRead), .out_4(decoder_1_out_4), .out_8(MemWrite), .out_12(ALUOp[1]),
    .out_24(ALUOp[0]));  // open: out_1, out_2, out_3, out_5, out_6, out_7, out_9, out_10, out_11, out_13, out_14, out_15, out_16, out_17, out_18, out_19, out_20, out_21, out_22, out_23, out_25, out_26, out_27, out_28, out_29, out_30, out_31
  or or_1 (RegWrite, MemRead, decoder_1_out_4, ALUOp[1]);
  or or_2 (ALUSrc, decoder_1_out_4, MemWrite, MemRead);

  assign Branch = ALUOp[0];
  assign func7 = inst[31:25];
  assign funct3 = inst[14:12];
  assign imm = inst[31:20];
  assign inst_31_0 = inst;
  assign MemToReg = MemRead;
  assign opcode_6_0 = inst[6:0];
  assign rd_inst_11_7 = inst[11:7];
  assign rs1_inst_19_15 = inst[19:15];
  assign rs2_inst_24_20 = inst[24:20];

  // Notes on the sheet:
  //   INSTRUCTION DECODER - CONTROL BLOCK
  //   Load
  //   Store
  //   Itype
  //   Rtype
endmodule
