// Digital circuit RegisterFile.dig as structural Verilog
module RegisterFile (
  input  [31:0] write_data,
  input  [31:0] _0,
  input  [31:0] tmp1,
  input  [4:0] rd_inst_11_7,
  input  [4:0] rs1_inst_19_15,
  input  [4:0] rs2_inst_24_20,
  input  [31:0] tmp2,
  input  clk,
  input  RegWrite,
  input  [31:0] _0_32,
  output [31:0] Read_Data1,
  output [31:0] Read_Data2
);

  wire decoder_1_out_0, decoder_1_out_1, decoder_1_out_2, decoder_1_out_3, decoder_1_out_4, decoder_1_out_5,
       decoder_1_out_6, decoder_1_out_7;
  wire [31:0] multiplexer_1_out, multiplexer_2_out, multiplexer_3_out, multiplexer_4_out, multiplexer_5_out,
       multiplexer_6_out, multiplexer_7_out, R0_q, R1_q, R2_q, R3_q, R4_q, R5_q, R6_q, R7_q;

  Decoder #(.Selector_Bits(5)) decoder_1 (
    .sel(rd_inst_11_7), .out_0(decoder_1_out_0), .out_1(decoder_1_out_1), .out_2(decoder_1_out_2),
    .out_3(decoder_1_out_3), .out_4(decoder_1_out_4), .out_5(decoder_1_out_5), .out_6(decoder_1_out_6),
    .out_7(decoder_1_out_7));  // open: out_8, out_9, out_10, out_11, out_12, out_13, out_14, out_15, out_16, out_17, out_18, out_19, out_20, out_21, out_22, out_23, out_24, out_25, out_26, out_27, out_28, out_29, out_30, out_31
  Register #(.Bits(32)) R0 (.D(_0), .C(clk), .en(decoder_1_out_0), .Q(R0_q));
  Register #(.Bits(32)) R4 (.D(multiplexer_1_out), .C(clk), .en(decoder_1_out_4), .Q(R4_q));
  Multiplexer #(.Bits(32)) multiplexer_1 (.sel(RegWrite), .in_0(R4_q), .in_1(write_data), .out(multiplexer_1_out));
  Register #(.Bits(32)) R1 (.D(multiplexer_2_out), .C(clk), .en(decoder_1_out_1), .Q(R1_q));
  Register #(.Bits(32)) R5 (.D(multiplexer_3_out), .C(clk), .en(decoder_1_out_5), .Q(R5_q));
  Multiplexer #(.Bits(32)) multiplexer_2 (.sel(RegWrite), .in_0(R1_q), .in_1(write_data), .out(multiplexer_2_out));
  Multiplexer #(.Bits(32)) multiplexer_3 (.sel(RegWrite), .in_0(R5_q), .in_1(write_data), .out(multiplexer_3_out));
  Register #(.Bits(32)) R2 (.D(multiplexer_5_out), .C(clk), .en(decoder_1_out_2), .Q(R2_q));
  Multiplexer #(.Bits(32)) multiplexer_4 (.sel(RegWrite), .in_0(R6_q), .in_1(write_data), .out(multiplexer_4_out));
  Register #(.Bits(32)) R6 (.D(multiplexer_4_out), .C(clk), .en(decoder_1_out_6), .Q(R6_q));
  Multiplexer #(.Bits(32)) multiplexer_5 (.sel(RegWrite), .in_0(R2_q), .in_1(write_data), .out(multiplexer_5_out));
  Register #(.Bits(32)) R3 (.D(multiplexer_7_out), .C(clk), .en(decoder_1_out_3), .Q(R3_q));
  Register #(.Bits(32)) R7 (.D(multiplexer_6_out), .C(clk), .en(decoder_1_out_7), .Q(R7_q));
  Multiplexer #(.Bits(32)) multiplexer_6 (.sel(RegWrite), .in_0(R7_q), .in_1(write_data), .out(multiplexer_6_out));
  Multiplexer #(.Bits(32)) multiplexer_7 (.sel(RegWrite), .in_0(R3_q), .in_1(write_data), .out(multiplexer_7_out));
  Multiplexer #(.Selector_Bits(5), .Bits(32)) multiplexer_8 (
    .sel(rs1_inst_19_15), .in_0(R0_q), .in_1(R1_q), .in_2(R2_q), .in_3(R3_q), .in_4(R4_q), .in_5(R5_q),
    .in_6(R6_q), .in_7(R7_q), .in_8(tmp1), .in_9(tmp1), .in_10(tmp1), .in_11(tmp1), .in_12(tmp1),
    .in_13(tmp1), .in_14(tmp1), .in_15(tmp1), .in_16(tmp1), .in_17(tmp1), .in_18(tmp1), .in_19(tmp1),
    .in_20(tmp1), .in_21(tmp1), .in_22(tmp1), .in_23(tmp1), .in_24(tmp1), .in_25(tmp1), .in_26(tmp1),
    .in_27(tmp1), .in_28(tmp1), .in_29(tmp1), .in_30(tmp1), .in_31(tmp1), .out(Read_Data1));
  Multiplexer #(.Selector_Bits(5), .Bits(32)) multiplexer_9 (
    .sel(rs2_inst_24_20), .in_0(R0_q), .in_1(R1_q), .in_2(R2_q), .in_3(R3_q), .in_4(R4_q), .in_5(R5_q),
    .in_6(R6_q), .in_7(R7_q), .in_8(tmp2), .in_9(tmp2), .in_10(tmp2), .in_11(tmp2), .in_12(tmp2),
    .in_13(tmp2), .in_14(tmp2), .in_15(tmp2), .in_16(tmp2), .in_17(tmp2), .in_18(tmp2), .in_19(tmp2),
    .in_20(tmp2), .in_21(tmp2), .in_22(tmp2), .in_23(tmp2), .in_24(tmp2), .in_25(tmp2), .in_26(tmp2),
    .in_27(tmp2), .in_28(tmp2), .in_29(tmp2), .in_30(tmp2), .in_31(tmp2), .out(Read_Data2));

  // Other names for the same wires on the sheet: data_in[31:0] = write_data; reg_wr = RegWrite; z_t[31:0] = _0_32

  // Notes on the sheet:
  //   write_data: default 2314226
  //   rd_inst_11_7: default 5
endmodule
