// Digital circuit riscv_version3.dig as structural Verilog
module riscv_version3 (
  input  [31:0] _0_32,
  input  [31:0] A,
  input  [31:0] _0_33,
  output Y,
  output [31:0] X,
  output [31:0] Z,
  output [3:0] U,
  output [31:0] V,
  output [5:0] Y2,
  output [23:0] X2
);

  wire ALUSrc, Clock, CONTROL_BLOCK_memread, CONTROL_BLOCK_memwrite, CONTROL_BLOCK_regwrite, MemToReg;
  wire [1:0] CONTROL_BLOCK_aluop;
  wire [2:0] fc3;
  wire [4:0] CONTROL_BLOCK_rd_inst_11_7, CONTROL_BLOCK_rs1_inst_19_15, CONTROL_BLOCK_rs2_inst_24_20;
  wire [6:0] fc7;
  wire [23:0] PC_out;
  wire [31:0] CONTROL_BLOCK_inst_31_0, IMMEDIATE_GENERATION_immidiate, multiplexer_1_out, multiplexer_3_out,
       PROGRAM_MEMORY_d, REGISTER_FILE___only_r0_r8_done_read_data1,
       REGISTER_FILE___only_r0_r8_done_read_data2;

  Counter #(.Bits(24)) PC (.en(1'b1), .C(Clock), .clr(1'b0), .out(PC_out), .ovf(Y));
  ROM #(.AddrBits(24), .isProgramMemory("true"), .Bits(32)) PROGRAM_MEMORY (
    .A(PC_out), .sel(1'b1), .D(PROGRAM_MEMORY_d));
  InstructionDecoder CONTROL_BLOCK (
    .inst(PROGRAM_MEMORY_d), .rd_inst_11_7(CONTROL_BLOCK_rd_inst_11_7),
    .rs1_inst_19_15(CONTROL_BLOCK_rs1_inst_19_15), .rs2_inst_24_20(CONTROL_BLOCK_rs2_inst_24_20),
    .func7(fc7),
    .inst_31_0({CONTROL_BLOCK_inst_31_0[31], U[3], CONTROL_BLOCK_inst_31_0[29:15], U[2:0], CONTROL_BLOCK_inst_31_0[11:0]}),
    .funct3(fc3), .MemRead(CONTROL_BLOCK_memread), .MemToReg(MemToReg), .ALUOp(CONTROL_BLOCK_aluop),
    .MemWrite(CONTROL_BLOCK_memwrite), .ALUSrc(ALUSrc), .RegWrite(CONTROL_BLOCK_regwrite));  // open: opcode_6_0, imm, Branch
  Button button_1 (.out(Clock));
  // Probe on PC_out
  RegisterFile REGISTER_FILE___only_r0_r8_done (
    .write_data(multiplexer_3_out), ._0(_0_32), .tmp1(_0_32), .rd_inst_11_7(CONTROL_BLOCK_rd_inst_11_7),
    .rs1_inst_19_15(CONTROL_BLOCK_rs1_inst_19_15), .rs2_inst_24_20(CONTROL_BLOCK_rs2_inst_24_20),
    .tmp2(_0_32), .clk(Clock), .RegWrite(CONTROL_BLOCK_regwrite), ._0_32(_0_33),
    .Read_Data1(REGISTER_FILE___only_r0_r8_done_read_data1),
    .Read_Data2(REGISTER_FILE___only_r0_r8_done_read_data2));
  ImmediateGen IMMEDIATE_GENERATION (
    .instr({CONTROL_BLOCK_inst_31_0[31], U[3], CONTROL_BLOCK_inst_31_0[29:15], U[2:0], CONTROL_BLOCK_inst_31_0[11:0]}),
    .immidiate(IMMEDIATE_GENERATION_immidiate));
  Alu_Control_Unit ALU_CONTROL_UNIT (.Control_in(U), .Alu_op(CONTROL_BLOCK_aluop), .Operation(Y2));
  Multiplexer #(.Bits(32)) multiplexer_1 (
    .sel(ALUSrc), .in_0(REGISTER_FILE___only_r0_r8_done_read_data2), .in_1(IMMEDIATE_GENERATION_immidiate),
    .out(multiplexer_1_out));
  BarrelShifter #(.Bits(32), .barrelSigned("true")) ShiftLeft1 (
    .in(IMMEDIATE_GENERATION_immidiate), .shift(7'b0000001), .out(Z));
  ALU ALU (
    .operation(Y2), .src1(REGISTER_FILE___only_r0_r8_done_read_data1), .src2(multiplexer_1_out), .func3(fc3),
    .func7(fc7), .Result(V));  // open: Zero, Overflow, CarryOut
  Multiplexer #(.Bits(32)) multiplexer_2 (.sel(1'b0), .in_0(A), .in_1(Z));  // open: out
  EEPROMDualPort #(.AddrBits(24), .Bits(32)) MAIN_MEMORY (
    .A(V[23:0]), .Din(REGISTER_FILE___only_r0_r8_done_read_data2), .str(CONTROL_BLOCK_memwrite), .C(Clock),
    .ld(CONTROL_BLOCK_memread), .D(X));
  Multiplexer #(.Bits(32)) multiplexer_3 (.sel(MemToReg), .in_0(V), .in_1(X), .out(multiplexer_3_out));

  assign X2 = V[23:0];

  // Notes on the sheet:
  //   Implemented instructions: 
  //   ADD, SUB, SW, LW, SLL, SRL, SRA, XOR
  //   MUL, OR, AND, SLT, SLTU, addi
  //   TESTfile
  //   0.lw x1,0(x0)
  //      1. lw x2,1(x0)
  //       2.add x3, x1, x2
  //       3.sw x3, 2 (x0) 
  //   4.add x1, x1, x0
  //      5. sub x4, x2, x1
  //       6.sw x4, 3(x0)
  //       7.add x1, x1, x0
  //       8.lw x1, 9(x0)
  //       9.lw x2, 10(x0)
  //       10.sll x3, x1, x2
  //       11.sw x3, 8(x0)
  //       12. srl x3,x1,x2
  //       13. sw x3, 12(x0)
  //       14, sra x3, x1, x2
  //       15. sw x3, 16(x0)
  //       16. xor x3, x1, x2
  //       17. sw x3,20(x0)
  //       18. mul x3, x2, x1
  //       19. sw x3, 24(x0)
  //       20. or x3, x2, x1
  //       21. sw x3, 28(x0)
  //   22.  and x3, x2, x1
  //   23.  sw x3, 29(x0)
  //   24.  slt x3, x2, x1
  //   25.  sw x3, 30(x0)
  //   26.  sltu x3, x2, x1
  //   27.  sw x3, 31(x0)
  //   28.  addi x4, x3, -3
  //   29.   sw x4, 32(x0)
  //   contents of PROGRAM_MEMORY (hex, n*v repeats v):
  //   2083,102103,2081b3,302123,80b3,40110233,4021a3,80b3,902083,a02103
  //   ,2091b3,302423,20d1b3,302623,4020d1b3,302823,20c1b3,302a23,21101b3
  //   ,302c23,1161b3,302e23,1171b3,302ea3,1121b3,302f23,1131b3,302fa3
  //   ,ffd18213,2402023
  //   RISCV32I CPU
  //   contents of MAIN_MEMORY (hex, n*v repeats v):
  //   22,37,59,15,4*0,24,9,2,0,2,0,0,0,2,0,0,0,b,0,0,0,12,0,0,0,b,0
  //   ,1,1,fffffffe
endmodule
